// Logisim project w4_counter.circ as structural Verilog: 1 circuit, main circuit main
module main (
  input  [15:0] in,
  input  increment,
  input  load,
  input  reset,
  output [15:0] out
);

  wire clock_1_out, or_1_out;
  wire [15:0] adder_1_out, multiplexer_1_out;

  Adder #(.width(16)) adder_1 (.a(out), .b(16'h1), .out(adder_1_out));  // open: cin, cout
  Multiplexer #(.select(3), .width(16)) multiplexer_1 (
    .in0(out), .in1(adder_1_out), .in2(in), .in4({16{1'b0}}), .out(multiplexer_1_out),
    .sel({reset, load, increment}), .en(1'b1));  // open: in3, in5, in6, in7
  or or_1 (or_1_out, increment, load, reset);
  Register #(.width(16)) register_1 (.D(multiplexer_1_out), .en(or_1_out), .Q(out), .clk(clock_1_out));  // open: clr
  Clock clock_1 (.out(clock_1_out));
endmodule
